// Logisim project CRC-AC.circ as structural Verilog: 2 circuits, main circuit CRC
module CRC (
  input  [7:0] A,
  input  [3:0] B,
  output [10:0] C
);

  wire [2:0] divider_1_remained, divider_2_remained, divider_3_remained, divider_4_remained,
       divider_5_remained, divider_6_remained, divider_7_remained;

  divider divider_1 (.dividend(A[7:4]), .divisor(B), .remained(divider_1_remained));  // open: quotient
  divider divider_2 (
    .dividend({divider_1_remained, A[3]}), .divisor(B), .remained(divider_2_remained));  // open: quotient
  divider divider_3 (
    .dividend({divider_2_remained, A[2]}), .divisor(B), .remained(divider_3_remained));  // open: quotient
  divider divider_4 (
    .dividend({divider_3_remained, A[1]}), .divisor(B), .remained(divider_4_remained));  // open: quotient
  divider divider_5 (
    .dividend({divider_4_remained, A[0]}), .divisor(B), .remained(divider_5_remained));  // open: quotient
  divider divider_6 (
    .dividend({divider_5_remained, 1'b0}), .divisor(B), .remained(divider_6_remained));  // open: quotient
  divider divider_7 (
    .dividend({divider_6_remained, 1'b0}), .divisor(B), .remained(divider_7_remained));  // open: quotient
  divider divider_8 (.dividend({divider_7_remained, 1'b0}), .divisor(B), .remained(C[2:0]));  // open: quotient

  assign C[10:3] = A;
endmodule

module divider (
  input  [3:0] dividend,
  input  [3:0] divisor,
  output quotient,
  output [2:0] remained
);

  wire and_1_out, not_1_out, not_2_out;
  wire [3:0] multiplexer_1_out, xor_1_out;

  not not_1 (not_1_out, dividend[3]);
  not not_2 (not_2_out, divisor[3]);
  and and_1 (and_1_out, not_1_out, not_2_out);
  or or_1 (quotient, dividend[3], and_1_out);
  Multiplexer #(.width(4), .enable("false")) multiplexer_1 (
    .in0(4'b0000), .in1(divisor), .out(multiplexer_1_out), .sel(quotient));
  assign xor_1_out = dividend ^ multiplexer_1_out;  // XOR_Gate xor_1, 4 bits wide
  Bit_Extender #(.in_width(4), .out_width(3)) bit_extender_1 (.in(xor_1_out), .out(remained));
endmodule
