// Logisim project fsm-AC.circ as structural Verilog: 2 circuits, main circuit fsm
module fsm (
  input  [1:0] IN,
  input  CLR,
  output Z
);

  wire CLK_out;
  wire [2:0] multiplexer_1_out, next_1_next, register_1_q;

  Multiplexer #(.width(3)) multiplexer_1 (
    .in0(next_1_next), .in1(3'b000), .out(multiplexer_1_out), .sel(CLR));  // open: en
  Clock CLK (.out(CLK_out));
  Register #(.width(3)) register_1 (.D(multiplexer_1_out), .Q(register_1_q), .clk(CLK_out));  // open: en, clr
  next next_1 (.IN(IN), .NOW(register_1_q), .NEXT(next_1_next), .Z(Z));
endmodule

module next (
  input  [1:0] IN,
  input  [2:0] NOW,
  output [2:0] NEXT,
  output Z
);

  wire decoder_1_out1, decoder_1_out4, decoder_1_out5, decoder_1_out6, decoder_1_out8, decoder_1_out9,
       decoder_1_out10, decoder_1_out12, decoder_1_out13, decoder_1_out14, decoder_1_out16, decoder_1_out17,
       decoder_1_out18, decoder_1_out19, not_1_out;

  Decoder #(.select(5), .enable("false")) decoder_1 (
    .out1(decoder_1_out1), .out4(decoder_1_out4), .out5(decoder_1_out5), .out6(decoder_1_out6),
    .out8(decoder_1_out8), .out9(decoder_1_out9), .out10(decoder_1_out10), .out12(decoder_1_out12),
    .out13(decoder_1_out13), .out14(decoder_1_out14), .out16(decoder_1_out16), .out17(decoder_1_out17),
    .out18(decoder_1_out18), .out19(decoder_1_out19), .sel({NOW, IN}));  // open: out0, out2, out3, out7, out11, out15, out20, out21, out22, out23, out24, out25, out26, out27, out28, out29, out30, out31
  not not_1 (not_1_out, IN[0]);
  and and_1 (Z, not_1_out, NOW[0], NOW[1]);
  // OR_Gate or_1 has open pins: in0=decoder_1_out17, in1=decoder_1_out16, in2=decoder_1_out18, in3=decoder_1_out19, out=open
  or or_2 (NEXT[0], decoder_1_out6, decoder_1_out4, decoder_1_out10, decoder_1_out8, decoder_1_out1, decoder_1_out9, decoder_1_out13, decoder_1_out17);
  or or_3 (NEXT[1], decoder_1_out4, decoder_1_out5, decoder_1_out6, decoder_1_out8, decoder_1_out10);
  or or_4 (NEXT[2], decoder_1_out12, decoder_1_out14);
endmodule
