// Logisim project ftoi.circ as structural Verilog: 2 circuits, main circuit ftoi
module ftoi (
  input  [15:0] float,
  output [31:0] \int 
);

  wire comparator_1_eq, comparator_2_eq, normal;
  wire [4:0] e;
  wire [9:0] adder_1_out, m;
  wire [31:0] tran_1_int;

  \tran  tran_1 (.s(float[15]), .e(e), .m(m), .normal(normal), .\int (tran_1_int));
  Comparator #(.width(5)) comparator_1 (.a(float[14:10]), .b({5{1'b1}}), .eq(comparator_1_eq));  // open: gt, lt
  Multiplexer #(.width(32), .enable("false")) multiplexer_1 (
    .in0(tran_1_int), .in1({32{1'b0}}), .out(\int ), .sel(comparator_1_eq));
  Adder #(.width(10)) adder_1 (.a(float[9:0]), .b(10'h1), .out(adder_1_out));  // open: cin, cout
  Subtractor #(.width(5)) subtractor_1 (.a(float[14:10]), .b(5'b01111), .out(e));  // open: bin, bout
  Multiplexer #(.width(10), .enable("false")) multiplexer_2 (
    .in0(float[9:0]), .in1(adder_1_out), .out(m), .sel(comparator_2_eq));
  not not_1 (normal, comparator_2_eq);
  Comparator #(.width(5)) comparator_2 (.a(float[14:10]), .b({5{1'b0}}), .eq(comparator_2_eq));  // open: gt, lt

  // Other names for the same wires on the sheet: fra[9:0] = float[9:0]; exp[4:0] = float[14:10]; s = float[15];
  //   sig = float[15]
endmodule

module \tran  (
  input  s,
  input  [4:0] e,
  input  [9:0] m,
  input  normal,
  output [31:0] \int 
);

  Multiplexer #(.width(32), .enable("false")) multiplexer_1 (.sel(normal));  // open: in0, in1, out
endmodule
