// Logisim project navigation-AC.circ as structural Verilog: 2 circuits, main circuit navigation
module navigation (
  input  [1:0] dir,
  input  clk,
  input  reset,
  output arrive,
  output hit
);

  wire next_1_arrive, next_1_hit;
  wire [2:0] next_1_next, state_q;

  Register #(.width(3)) state (.D(next_1_next), .Q(state_q), .clk(clk), .clr(reset));  // open: en
  next next_1 (.dir(dir), .now(state_q), .next(next_1_next), .arrive(next_1_arrive), .hit(next_1_hit));
  Register #(.width(1)) minus_ari (.D(next_1_arrive), .Q(arrive), .clk(clk), .clr(reset));  // open: en
  Register #(.width(1)) minus_hit (.D(next_1_hit), .Q(hit), .clk(clk), .clr(reset));  // open: en
endmodule

module next (
  input  [1:0] dir,
  input  [2:0] now,
  output [2:0] next,
  output arrive,
  output hit
);

  wire decoder_1_out0, decoder_1_out1, decoder_1_out2, decoder_1_out3, decoder_1_out8, decoder_1_out9,
       decoder_1_out10, decoder_1_out11, decoder_1_out12, decoder_1_out13, decoder_1_out15, decoder_1_out16,
       decoder_1_out17, decoder_1_out18, decoder_1_out19;

  Decoder #(.select(5)) decoder_1 (
    .out0(decoder_1_out0), .out1(decoder_1_out1), .out2(decoder_1_out2), .out3(decoder_1_out3),
    .out8(decoder_1_out8), .out9(decoder_1_out9), .out10(decoder_1_out10), .out11(decoder_1_out11),
    .out12(decoder_1_out12), .out13(decoder_1_out13), .out15(decoder_1_out15), .out16(decoder_1_out16),
    .out17(decoder_1_out17), .out18(decoder_1_out18), .out19(decoder_1_out19), .sel({now, dir}));  // open: out4, out5, out6, out7, out14, out20, out21, out22, out23, out24, out25, out26, out27, out28, out29, out30, out31, en
  or or_1 (next[0], decoder_1_out0, decoder_1_out9, decoder_1_out10, decoder_1_out15, decoder_1_out16, decoder_1_out19);
  or or_2 (next[1], decoder_1_out0, decoder_1_out8, decoder_1_out10, decoder_1_out11, decoder_1_out12, decoder_1_out15, decoder_1_out19);
  or or_3 (next[2], decoder_1_out13, decoder_1_out17, decoder_1_out18);
  or or_4 (arrive, decoder_1_out16, decoder_1_out9);
  or or_5 (hit, decoder_1_out18, decoder_1_out17, decoder_1_out15, decoder_1_out11, decoder_1_out8, decoder_1_out3, decoder_1_out2, decoder_1_out1);
endmodule
