// Logisim project qPlus.circ as structural Verilog: 12 circuits, main circuit Alu
// alu
module Alu (
  input  [31:0] A,
  input  [31:0] B,
  input  [4:0] ctrl,
  output bigger,
  output equal,
  output smaller,
  output [31:0] out
);

  wire [31:0] adder_1_out, adder_2_out, adder_3_out, and_1_out, multiplexer_1_out, or_1_out, shifter_1_out,
       subtractor_1_out;

  Comparator #(.width(32), .mode("unsigned")) comparator_1 (.a(A), .b(B), .gt(bigger), .eq(equal), .lt(smaller));
  Adder #(.width(32)) adder_1 (.a(A), .b(B), .out(adder_1_out));  // open: cin, cout
  Subtractor #(.width(32)) subtractor_1 (.a(A), .b(B), .out(subtractor_1_out));  // open: bin, bout
  assign and_1_out = A & B;  // AND_Gate and_1, 32 bits wide
  assign or_1_out = A | B;  // OR_Gate or_1, 32 bits wide
  Shifter #(.width(32)) shifter_1 (.in(B), .\dist (5'b10000), .out(shifter_1_out));
  Adder #(.width(32)) adder_2 (.a(A), .b(B), .out(adder_2_out));  // open: cin, cout
  Adder #(.width(32)) adder_3 (.a(adder_2_out), .b(32'hffff0000), .out(adder_3_out));  // open: cin, cout
  Multiplexer #(.width(32), .enable("false")) multiplexer_1 (
    .in0(adder_2_out), .in1(adder_3_out), .out(multiplexer_1_out), .sel(B[15]));
  Multiplexer #(.select(5), .width(32), .enable("false")) multiplexer_2 (
    .in0(adder_1_out), .in1(subtractor_1_out), .in4(and_1_out), .in5(or_1_out), .in6(shifter_1_out),
    .in7(multiplexer_1_out), .out(out), .sel(ctrl));  // open: in2, in3, in8, in9, in10, in11, in12, in13, in14, in15, in16, in17, in18, in19, in20, in21, in22, in23, in24, in25, in26, in27, in28, in29, in30, in31
endmodule

// grf
module Grf (
  input  clk,
  input  reset,
  input  wEn,
  input  [31:0] wD,
  input  [4:0] wA,
  input  [4:0] rA1,
  input  [4:0] rA2,
  output [31:0] rD1,
  output [31:0] rD2
);

  wire [31:0] in0, in1, in2, in3, in4, in5, in6, in7, in8, in9, in10, in11, in12, in13, in14, in15, in16,
       in17, in18, in19, in20, in21, in22, in23, in24, in25, in26, in27, in28, in29, in30, in31, out0, out1,
       out2, out3, out4, out5, out6, out7, out8, out9, out10, out11, out12, out13, out14, out15, out16,
       out17, out18, out19, out20, out21, out22, out23, out24, out25, out26, out27, out28, out29, out30,
       out31;

  Demultiplexer #(.select(5), .width(32), .tristate("true"), .enable("false")) demultiplexer_1 (
    .out0(in0), .out1(in1), .out2(in2), .out3(in3), .out4(in4), .out5(in5), .out6(in6), .out7(in7),
    .out8(in8), .out9(in9), .out10(in10), .out11(in11), .out12(in12), .out13(in13), .out14(in14),
    .out15(in15), .out16(in16), .out17(in17), .out18(in18), .out19(in19), .out20(in20), .out21(in21),
    .out22(in22), .out23(in23), .out24(in24), .out25(in25), .out26(in26), .out27(in27), .out28(in28),
    .out29(in29), .out30(in30), .out31(in31), .in(wD), .sel(wA));
  Multiplexer #(.select(5), .width(32), .enable("false")) multiplexer_1 (
    .in0(out0), .in1(out1), .in2(out2), .in3(out3), .in4(out4), .in5(out5), .in6(out6), .in7(out7),
    .in8(out8), .in9(out9), .in10(out10), .in11(out11), .in12(out12), .in13(out13), .in14(out14),
    .in15(out15), .in16(out16), .in17(out17), .in18(out18), .in19(out19), .in20(out20), .in21(out21),
    .in22(out22), .in23(out23), .in24(out24), .in25(out25), .in26(out26), .in27(out27), .in28(out28),
    .in29(out29), .in30(out30), .in31(out31), .out(rD1), .sel(rA1));
  Multiplexer #(.select(5), .width(32), .enable("false")) multiplexer_2 (
    .in0(out0), .in1(out1), .in2(out2), .in3(out3), .in4(out4), .in5(out5), .in6(out6), .in7(out7),
    .in8(out8), .in9(out9), .in10(out10), .in11(out11), .in12(out12), .in13(out13), .in14(out14),
    .in15(out15), .in16(out16), .in17(out17), .in18(out18), .in19(out19), .in20(out20), .in21(out21),
    .in22(out22), .in23(out23), .in24(out24), .in25(out25), .in26(out26), .in27(out27), .in28(out28),
    .in29(out29), .in30(out30), .in31(out31), .out(rD2), .sel(rA2));
  Register #(.width(32)) register_1 (.D({32{1'b0}}), .en(wEn), .Q(out0), .clk(clk), .clr(reset));
  Register #(.width(32)) register_2 (.D(in4), .en(wEn), .Q(out4), .clk(clk), .clr(reset));
  Register #(.width(32)) register_3 (.D(in8), .en(wEn), .Q(out8), .clk(clk), .clr(reset));
  Register #(.width(32)) register_4 (.D(in12), .en(wEn), .Q(out12), .clk(clk), .clr(reset));
  Register #(.width(32)) register_5 (.D(in16), .en(wEn), .Q(out16), .clk(clk), .clr(reset));
  Register #(.width(32)) register_6 (.D(in20), .en(wEn), .Q(out20), .clk(clk), .clr(reset));
  Register #(.width(32)) register_7 (.D(in24), .en(wEn), .Q(out24), .clk(clk), .clr(reset));
  Register #(.width(32)) register_8 (.D(in28), .en(wEn), .Q(out28), .clk(clk), .clr(reset));
  Register #(.width(32)) register_9 (.D(in1), .en(wEn), .Q(out1), .clk(clk), .clr(reset));
  Register #(.width(32)) register_10 (.D(in5), .en(wEn), .Q(out5), .clk(clk), .clr(reset));
  Register #(.width(32)) register_11 (.D(in9), .en(wEn), .Q(out9), .clk(clk), .clr(reset));
  Register #(.width(32)) register_12 (.D(in13), .en(wEn), .Q(out13), .clk(clk), .clr(reset));
  Register #(.width(32)) register_13 (.D(in17), .en(wEn), .Q(out17), .clk(clk), .clr(reset));
  Register #(.width(32)) register_14 (.D(in21), .en(wEn), .Q(out21), .clk(clk), .clr(reset));
  Register #(.width(32)) register_15 (.D(in25), .en(wEn), .Q(out25), .clk(clk), .clr(reset));
  Register #(.width(32)) register_16 (.D(in29), .en(wEn), .Q(out29), .clk(clk), .clr(reset));
  // Probe on in3
  Register #(.width(32)) register_17 (.D(in2), .en(wEn), .Q(out2), .clk(clk), .clr(reset));
  Register #(.width(32)) register_18 (.D(in6), .en(wEn), .Q(out6), .clk(clk), .clr(reset));
  Register #(.width(32)) register_19 (.D(in10), .en(wEn), .Q(out10), .clk(clk), .clr(reset));
  Register #(.width(32)) register_20 (.D(in14), .en(wEn), .Q(out14), .clk(clk), .clr(reset));
  Register #(.width(32)) register_21 (.D(in18), .en(wEn), .Q(out18), .clk(clk), .clr(reset));
  Register #(.width(32)) register_22 (.D(in22), .en(wEn), .Q(out22), .clk(clk), .clr(reset));
  Register #(.width(32)) register_23 (.D(in26), .en(wEn), .Q(out26), .clk(clk), .clr(reset));
  Register #(.width(32)) register_24 (.D(in30), .en(wEn), .Q(out30), .clk(clk), .clr(reset));
  Register #(.width(32)) register_25 (.D(in3), .en(wEn), .Q(out3), .clk(clk), .clr(reset));
  Register #(.width(32)) register_26 (.D(in7), .en(wEn), .Q(out7), .clk(clk), .clr(reset));
  Register #(.width(32)) register_27 (.D(in11), .en(wEn), .Q(out11), .clk(clk), .clr(reset));
  Register #(.width(32)) register_28 (.D(in15), .en(wEn), .Q(out15), .clk(clk), .clr(reset));
  Register #(.width(32)) register_29 (.D(in19), .en(wEn), .Q(out19), .clk(clk), .clr(reset));
  Register #(.width(32)) register_30 (.D(in23), .en(wEn), .Q(out23), .clk(clk), .clr(reset));
  Register #(.width(32)) register_31 (.D(in27), .en(wEn), .Q(out27), .clk(clk), .clr(reset));
  Register #(.width(32)) register_32 (.D(in31), .en(wEn), .Q(out31), .clk(clk), .clr(reset));

  // Other names for the same wires on the sheet: rst = reset; we = wEn
endmodule

// ctrl
module Controller (
  input  [5:0] op,
  input  [5:0] low6,
  output ifWrGrf,
  output ifWrRt,
  output [4:0] aluCtrl,
  output ifImmExt,
  output ifReDm,
  output ifWrDm,
  output ifBeq,
  output ifJal,
  output ifJr
);

  wire addu, lui, not_1_out, not_2_out, not_3_out, not_4_out, not_5_out, not_6_out, not_7_out, not_8_out,
       not_9_out, not_10_out, not_11_out, not_12_out, not_13_out, not_14_out, not_15_out, not_16_out,
       not_17_out, not_18_out, not_19_out, not_20_out, not_21_out, not_22_out, not_23_out, not_24_out,
       not_25_out, not_26_out, not_27_out, not_28_out, not_29_out, not_30_out, not_31_out, not_32_out,
       not_33_out, not_34_out, not_35_out, not_36_out, not_37_out, not_38_out, not_39_out, not_40_out,
       not_41_out, not_42_out, not_43_out, not_44_out, not_45_out, not_46_out, not_47_out, not_48_out,
       not_49_out, ori, subu;
  wire [7:7] or_1_out;

  not not_1 (not_1_out, op[4]);
  not not_2 (not_2_out, op[1]);
  not not_3 (not_3_out, op[3]);
  not not_4 (not_4_out, op[2]);
  not not_5 (not_5_out, op[5]);
  not not_6 (not_6_out, low6[2]);
  not not_7 (not_7_out, low6[3]);
  not not_8 (not_8_out, low6[1]);
  not not_9 (not_9_out, op[0]);
  not not_10 (not_10_out, low6[4]);
  and u_addu (addu, not_5_out, not_1_out, not_3_out, not_4_out, not_2_out, not_9_out, low6[5], not_10_out, not_7_out, not_6_out, not_8_out, low6[0]);
  not not_11 (not_11_out, op[0]);
  not not_12 (not_12_out, op[5]);
  not not_13 (not_13_out, op[4]);
  not not_14 (not_14_out, op[1]);
  not not_15 (not_15_out, op[2]);
  not not_16 (not_16_out, op[3]);
  and u_subu (subu, not_12_out, not_13_out, not_16_out, not_15_out, not_14_out, not_11_out, low6[5], not_19_out, not_18_out, not_17_out, low6[1], low6[0]);
  not not_17 (not_17_out, low6[2]);
  not not_18 (not_18_out, low6[3]);
  not not_19 (not_19_out, low6[4]);
  not not_20 (not_20_out, op[4]);
  not not_21 (not_21_out, op[5]);
  and u_ori (ori, not_21_out, not_20_out, op[3], op[2], not_22_out, op[0]);
  not not_22 (not_22_out, op[1]);
  not not_23 (not_23_out, op[2]);
  not not_24 (not_24_out, op[3]);
  not not_25 (not_25_out, op[4]);
  and lw (ifReDm, op[5], not_25_out, not_24_out, not_23_out, op[1], op[0]);
  or or_1 (or_1_out[7], ifReDm, ifWrDm);
  Coder coder_1 (.in({{24{1'b0}}, or_1_out[7], lui, ori, 3'b000, subu, addu}), .out(aluCtrl));
  not not_26 (not_26_out, op[4]);
  not not_27 (not_27_out, op[2]);
  and sw (ifWrDm, op[5], not_26_out, op[3], not_27_out, op[1], op[0]);
  not not_28 (not_28_out, op[3]);
  not not_29 (not_29_out, op[4]);
  not not_30 (not_30_out, op[1]);
  not not_31 (not_31_out, op[5]);
  and beq (ifBeq, not_31_out, not_29_out, not_28_out, op[2], not_30_out, not_32_out);
  not not_32 (not_32_out, op[0]);
  not not_33 (not_33_out, op[5]);
  not not_34 (not_34_out, op[4]);
  and u_lui (lui, not_33_out, not_34_out, op[3], op[2], op[1], op[0]);
  or or_2 (ifImmExt, lui, ori, ifReDm, ifWrDm);
  not not_35 (not_35_out, op[5]);
  not not_36 (not_36_out, op[4]);
  not not_37 (not_37_out, op[2]);
  not not_38 (not_38_out, op[3]);
  and jal (ifJal, not_35_out, not_36_out, not_38_out, not_37_out, op[1], op[0]);
  or or_3 (ifWrGrf, addu, subu, ifReDm, ori, lui, ifJal);
  or or_4 (ifWrRt, ori, lui, ifReDm);
  not not_39 (not_39_out, op[1]);
  not not_40 (not_40_out, op[5]);
  not not_41 (not_41_out, op[2]);
  not not_42 (not_42_out, op[0]);
  not not_43 (not_43_out, low6[5]);
  not not_44 (not_44_out, op[3]);
  not not_45 (not_45_out, op[4]);
  and jr (ifJr, not_40_out, not_45_out, not_44_out, not_41_out, not_39_out, not_42_out, not_43_out, not_46_out, low6[3], not_49_out, not_48_out, not_47_out);
  not not_46 (not_46_out, low6[4]);
  not not_47 (not_47_out, low6[0]);
  not not_48 (not_48_out, low6[1]);
  not not_49 (not_49_out, low6[2]);

  // Other names for the same wires on the sheet: beq = ifBeq; jal = ifJal; jr = ifJr; lw = ifReDm; sw = ifWrDm
endmodule

// dm
module Dm (
  input  ReadEnable,
  input  WriteEnable,
  input  [31:0] Addr,
  input  [31:0] WriteData,
  input  clk,
  output [31:0] ReadData
);

  wire [4:0] bit_extender_1_out;
  wire [31:0] shifter_1_out;

  Bit_Extender #(.in_width(32), .out_width(5)) bit_extender_1 (.in(shifter_1_out), .out(bit_extender_1_out));
  Shifter #(.width(32), .shift("lr")) shifter_1 (.in(Addr), .\dist (5'b00010), .out(shifter_1_out));
  RAM #(.addrWidth(5), .dataWidth(32), .bus("separate")) ram_1 (
    .addr(bit_extender_1_out), .din(WriteData), .data(ReadData), .str(WriteEnable), .clk(clk), .ld(ReadEnable));  // open: sel, clr
endmodule

module main (
  input  reset,
  output [31:0] Instr,
  output RegWrite,
  output [4:0] RegAddr,
  output [31:0] RegData,
  output MemWrite,
  output [4:0] MemAddr,
  output [31:0] MemData
);

  wire alu_bigger, alu_equal, alu_smaller, beq, clk, data_read, imm_ext_t, jal, jr, write_rt;
  wire [4:0] alu_ctrl, low5, rd, rs, rt;
  wire [5:0] low6, op;
  wire [15:0] imm;
  wire [25:0] jalTo;
  wire [31:0] alu_out, aluB, dm_out, grf1, ifuIn, imm_ext, pc, pcAdd4, shifter_1_out;

  Clock clock_1 (.out(clk));
  Ifu ifu_1 (.pcIn(ifuIn), .clk(clk), .reset(reset), .instr(Instr), .pcAdd4(pcAdd4), .pc(pc));
  assign imm_ext = {{16{1'b0}}, imm};  // Bit_Extender bit_extender_1
  AluBSel AluBSel (.grfRd2(MemData), .immExt(imm_ext), .ifImmExt(imm_ext_t), .out(aluB));
  InstrDecd instrdecd_1 (
    .pc(Instr), .op_31_26(op), .rs_25_21(rs), .rt_20_16(rt), .rd_15_11(rd), .low5_10_6(low5),
    .low6_5_0(low6), .immediate(imm), .jalTo(jalTo));
  grfWaSel grfWaSel (.rd(rd), .rt(rt), .ifWrRt(write_rt), .ifJal(jal), .out(RegAddr));
  GrfWdSel grfWdSel (.aluOut(alu_out), .ifReDm(data_read), .ifJal(jal), .dmOut(dm_out), .pcAdd4(pcAdd4), .out(RegData));
  Controller controller_1 (
    .op(op), .low6(low6), .ifWrGrf(RegWrite), .aluCtrl(alu_ctrl), .ifWrRt(write_rt), .ifImmExt(imm_ext_t),
    .ifReDm(data_read), .ifWrDm(MemWrite), .ifBeq(beq), .ifJal(jal), .ifJr(jr));
  IfuInSel ifuInSel (
    .ifJr(jr), .grfRD1(grf1), .ifJal(jal), .ifBeq(beq), .jalTo(jalTo), .ifEqual(alu_equal), .pc(pc),
    .pcAdd4(pcAdd4), .immExt(imm_ext), .out(ifuIn));
  Grf grf_1 (
    .clk(clk), .reset(reset), .wEn(RegWrite), .wD(RegData), .wA(RegAddr), .rD1(grf1), .rD2(MemData),
    .rA1(rs), .rA2(rt));
  Alu alu_1 (
    .A(grf1), .B(aluB), .out(alu_out), .ctrl(alu_ctrl), .bigger(alu_bigger), .equal(alu_equal),
    .smaller(alu_smaller));
  Dm dm_1 (
    .Addr(alu_out), .WriteData(MemData), .ReadData(dm_out), .ReadEnable(data_read), .WriteEnable(MemWrite),
    .clk(clk));
  Shifter #(.width(32), .shift("lr")) shifter_1 (.in(alu_out), .\dist (5'b00010), .out(shifter_1_out));
  Bit_Extender #(.in_width(32), .out_width(5)) bit_extender_2 (.in(shifter_1_out), .out(MemAddr));

  // Other names for the same wires on the sheet: data_write = MemWrite; grf2[31:0] = MemData; grfWa[4:0] = RegAddr;
  //   grfWd[31:0] = RegData; GrfWrite = RegWrite
endmodule

// IFU
module Ifu (
  input  [31:0] pcIn,
  input  clk,
  input  reset,
  output [31:0] pcAdd4,
  output [31:0] pc,
  output [31:0] instr
);

  wire [4:0] bit_extender_1_out;
  wire [31:0] shifter_1_out;

  Register #(.width(32)) pcReg (.D(pcIn), .Q(pc), .clk(clk), .clr(reset));  // open: en
  Shifter #(.width(32), .shift("lr")) shifter_1 (.in(pc), .\dist (5'b00010), .out(shifter_1_out));
  Bit_Extender #(.in_width(32), .out_width(5)) bit_extender_1 (.in(shifter_1_out), .out(bit_extender_1_out));
  Adder #(.width(32)) adder_1 (.a(pc), .b(32'h4), .out(pcAdd4));  // open: cin, cout
  ROM #(.addrWidth(5), .dataWidth(32)) rom_1 (.addr(bit_extender_1_out), .data(instr));  // open: sel
endmodule

module InstrDecd (
  input  [31:0] pc,
  output [5:0] op_31_26,
  output [4:0] rs_25_21,
  output [4:0] rt_20_16,
  output [4:0] rd_15_11,
  output [4:0] low5_10_6,
  output [5:0] low6_5_0,
  output [15:0] immediate,
  output [25:0] jalTo
);


  assign immediate = pc[15:0];
  assign jalTo = pc[25:0];
  assign low5_10_6 = pc[10:6];
  assign low6_5_0 = pc[5:0];
  assign op_31_26 = pc[31:26];
  assign rd_15_11 = pc[15:11];
  assign rs_25_21 = pc[25:21];
  assign rt_20_16 = pc[20:16];
endmodule

// trans
module Coder (
  input  [31:0] in,
  output [4:0] out
);

  or _0 (out[0], in[1], in[3], in[5], in[7], in[9], in[11], in[13], in[15], in[17], in[19], in[21], in[23], in[25], in[27], in[29], in[31]);
  or _1 (out[1], in[2], in[3], in[6], in[7], in[10], in[11], in[14], in[15], in[18], in[19], in[22], in[23], in[26], in[27], in[30], in[31]);
  or _2 (out[2], in[4], in[5], in[6], in[7], in[12], in[13], in[14], in[15], in[20], in[21], in[22], in[23], in[28], in[29], in[30], in[31]);
  or _3 (out[3], in[8], in[9], in[10], in[11], in[12], in[13], in[14], in[15], in[21], in[22], in[23], in[25], in[26], in[28], in[30], in[31]);
  or _4 (out[4], in[16], in[17], in[18], in[19], in[20], in[21], in[22], in[23], in[24], in[25], in[26], in[27], in[28], in[29], in[30], in[31]);
endmodule

module grfWaSel (
  input  [4:0] rd,
  input  [4:0] rt,
  input  ifWrRt,
  input  ifJal,
  output [4:0] out
);

  wire [4:0] multiplexer_1_out;

  Multiplexer #(.width(5), .enable("false")) multiplexer_1 (.in0(rd), .in1(rt), .out(multiplexer_1_out), .sel(ifWrRt));
  Multiplexer #(.width(5), .enable("false")) multiplexer_2 (
    .in0(multiplexer_1_out), .in1({5{1'b1}}), .out(out), .sel(ifJal));
endmodule

module GrfWdSel (
  input  [31:0] aluOut,
  input  ifReDm,
  input  ifJal,
  input  [31:0] dmOut,
  input  [31:0] pcAdd4,
  output [31:0] out
);

  wire [31:0] multiplexer_1_out;

  Multiplexer #(.width(32), .enable("false")) multiplexer_1 (
    .in0(aluOut), .in1(dmOut), .out(multiplexer_1_out), .sel(ifReDm));
  Multiplexer #(.width(32), .enable("false")) multiplexer_2 (
    .in0(multiplexer_1_out), .in1(pcAdd4), .out(out), .sel(ifJal));
endmodule

module AluBSel (
  input  [31:0] grfRd2,
  input  [31:0] immExt,
  input  ifImmExt,
  output [31:0] out
);

  Multiplexer #(.width(32), .enable("false")) multiplexer_1 (.in0(grfRd2), .in1(immExt), .out(out), .sel(ifImmExt));
endmodule

module IfuInSel (
  input  ifJr,
  input  [31:0] grfRD1,
  input  ifJal,
  input  ifBeq,
  input  [25:0] jalTo,
  input  ifEqual,
  input  [31:0] pc,
  input  [31:0] pcAdd4,
  input  [31:0] immExt,
  output [31:0] out
);

  wire and_1_out;
  wire [31:0] adder_1_out, adder_2_out, multiplexer_1_out, multiplexer_2_out, multiplexer_3_out,
       shifter_1_out;

  Multiplexer #(.width(32), .enable("false")) multiplexer_1 (
    .in0(pcAdd4), .in1(grfRD1), .out(multiplexer_1_out), .sel(ifJr));
  Adder #(.width(32)) adder_1 (.a(immExt), .b(32'hffff0000), .out(adder_1_out));  // open: cin, cout
  Multiplexer #(.width(32), .enable("false")) multiplexer_2 (
    .in0(immExt), .in1(adder_1_out), .out(multiplexer_2_out), .sel(immExt[15]));
  Multiplexer #(.width(32), .enable("false")) multiplexer_3 (
    .in0(multiplexer_1_out), .in1({pc[31:28], jalTo, 2'b00}), .out(multiplexer_3_out), .sel(ifJal));
  Adder #(.width(32)) adder_2 (.a(pcAdd4), .b(shifter_1_out), .out(adder_2_out));  // open: cin, cout
  Shifter #(.width(32)) shifter_1 (.in(multiplexer_2_out), .\dist (5'b00010), .out(shifter_1_out));
  and and_1 (and_1_out, ifBeq, ifEqual);
  Multiplexer #(.width(32), .enable("false")) multiplexer_4 (
    .in0(multiplexer_3_out), .in1(adder_2_out), .out(out), .sel(and_1_out));
endmodule
